# Fritzing sketch Tipsy_Schematic (saved by Fritzing 0.9.2b)
stripboards: 4

parts:
  Part1 = Motor Driver 1A Dual TB6612FNG  # not connected
  VCC1 = Battery  # not connected
  VCC2 = Battery
  IC1 = Voltage Regulator [package=to-220-alt]
  J3 = female pin header, 2 pins [form="♀ (female)"]
  J4 = female pin header, 2 pins [form="♀ (female)"]  # not connected
  J5 = female pin header, 2 pins [form="♀ (female)"]  # not connected
  J6 = female pin header, 2 pins [form="♀ (female)"]  # not connected
  J7 = female pin header, 2 pins [form="♀ (female)"]  # not connected
  J8 = female pin header, 2 pins [form="♀ (female)"]  # not connected
  J9 = female pin header, 2 pins [form="♀ (female)"]  # not connected
  J10 = female pin header, 2 pins [form="♀ (female)"]  # not connected

nets:
  N1: VCC2.-, IC1.IN, J3.pin2
  N2: VCC2.+, IC1.GND

notes:
  1
  5
  10
  15
  20
  30
  25
  50
  40
  35
  44
  55
  67
  65
  60
  45
  a     b     c     d     e
  f     g     h     i     j
  + -
  5v RAIL
  >5v RAIL
  VCC
  PORTx
  Rx6
  Rx2
  Rx4
  Rx0
  Rx1
  GND
  Rx3
  Rx5
  Rx7
  This establishes a common ground as discussed with Trud
  VIN
  DA
  CL
  NC
  AD0
  ADA
  FSNC
  ACL
  INT
  4
  6
  2
  3
  0
  7
  VPP
  RX
  TX
  PIN1: VPP
  PIN2: VCC
  PIN3: GND
  PIN4: RB7
  PIN6: NOT USED
  PIN5: RB6
  A01
  VM
  A02
  B01
  B02
  AI1
  AI2
  STBY
  PWMA
  BI1
  PWMB
  BI2
